# Fritzing sketch powerpi (saved by Fritzing 0.9.2b)
breadboards: 1

parts:
  SmartMeter = Smart Meter - S0-Bus
  RPi = Raspberry Pi B rev1
  R1 = Resistor [tolerance=±5% resistance=10k package=THT]

nets (from the breadboard view):
  N1: SmartMeter.S0a, RPi.GPIO_24, R1.Pin_1
  N2: SmartMeter.S0b, RPi.GND
  N3: RPi.3V3, R1.Pin_0

custom parts:
  Smart Meter - S0-Bus: SmartMeter with S0-Bus
