# Fritzing sketch powerpi (saved by Fritzing 0.9.2b)
circuit board: 8.46667cm x 5.64444cm
breadboards: 1

parts:
  Raspberry_Pi1 = Raspberry Pi B rev2
  R1 = Resistor [tolerance=±5% resistance=10k package=THT]
  S1 = Square Pushbutton

nets:
  N1: Raspberry_Pi1.3V3, R1.Pin_0
  N2: Raspberry_Pi1.GPIO_24, R1.Pin_1, S1.leg0, S1.leg1
